// Logisim project logisimBisectionMethod.circ as structural Verilog: 1 circuit, main circuit main
module main (
  input  go_i
);

  wire adder_1_p3, adder_2_p3, adder_3_p3, adder_4_p3, adder_5_p3, and_1_out, and_2_out, and_3_out,
       and_4_out, and_5_out, and_6_out, and_7_out, and_8_out, and_9_out, clock_1_out, comparator_1_p3,
       comparator_2_p3, comparator_2_p4, comparator_2_p5, comparator_3_p2, comparator_3_p3, comparator_3_p4,
       decoder_1_out0, decoder_1_out1, decoder_1_out2, decoder_1_out3, decoder_1_out4, decoder_1_out5,
       decoder_1_out6, decoder_1_out7, fp_const_2_p1, fp_const_4_p1, fp_const_5_p1, fp_const_6_p1,
       fp_const_7_p1, fp_const_8_p1, fp_const_10_p1, fp_const_11_p1, multiplier_1_p3, multiplier_2_p3,
       multiplier_3_p3, multiplier_4_p3, multiplier_5_p3, multiplier_6_p3, multiplier_7_p3, multiplier_8_p2,
       multiplier_9_p3, multiplier_10_p3, multiplier_11_p3, not_1_out, not_2_out, not_3_out, not_4_out,
       or_3_out, or_5_out, or_6_out, or_7_out, or_8_out, or_9_out;
  wire [2:0] or_4_out, register_1_q;
  wire [31:0] adder_1_p1, adder_1_p2, adder_6_p3, comparator_3_p1, divider_1_p3, fp_const_1_p1,
       fp_const_3_p1, multiplexer_1_out, multiplexer_2_out, multiplexer_3_out, multiplexer_4_out,
       multiplier_1_p1, multiplier_1_p2, multiplier_8_p3, register_3_q, register_7_q;

  not not_1 (not_1_out, register_1_q[2]);
  not not_2 (not_2_out, register_1_q[1]);
  not not_3 (not_3_out, register_1_q[0]);
  and and_1 (and_1_out, not_2_out, register_1_q[0]);
  and and_2 (and_2_out, register_1_q[2], register_1_q[1], not_3_out);
  and and_3 (and_3_out, not_1_out, not_2_out, go_i, not_3_out);
  and and_4 (and_4_out, register_1_q[2], not_2_out, not_3_out);
  Register #(.width(3)) register_1 (.D(or_4_out), .Q(register_1_q), .clk(clock_1_out));  // open: en, clr
  // FP_Const fp_const_1: pin names not known; wires that end beside it: fp_const_1_p1
  and and_5 (and_5_out, not_1_out, register_1_q[1], register_1_q[0]);
  and and_6 (and_6_out, not_1_out, register_1_q[1], not_3_out, or_5_out);
  and and_7 (and_7_out, not_1_out, register_1_q[1], not_3_out);
  // FP_Const fp_const_2: pin names not known; wires that end beside it: fp_const_2_p1
  Multiplexer #(.width(32)) multiplexer_1 (
    .in0(fp_const_1_p1), .in1(register_3_q), .out(multiplexer_1_out), .sel(decoder_1_out5));  // open: en
  // Adder adder_1: pin names not known; wires that end beside it: adder_1_p1, adder_1_p2, adder_1_p3
  // Divider divider_1: pin names not known; wires that end beside it: adder_1_p3, fp_const_2_p1, divider_1_p3
  Multiplexer #(.width(32)) multiplexer_2 (
    .in0(fp_const_1_p1), .in1(divider_1_p3), .out(multiplexer_2_out), .sel(decoder_1_out3));  // open: en
  or or_1 (or_4_out[2], and_4_out, and_5_out, and_6_out);
  and and_8 (and_8_out, and_4_out, or_3_out);
  and and_9 (and_9_out, and_4_out, comparator_2_p3);
  // FP_Const fp_const_3: pin names not known; wires that end beside it: fp_const_3_p1
  or or_2 (or_4_out[1], and_7_out, and_8_out, and_1_out, and_2_out);
  Multiplexer #(.width(32)) multiplexer_3 (
    .in0(fp_const_3_p1), .in1(register_3_q), .out(multiplexer_3_out), .sel(decoder_1_out6));  // open: en
  // FP_Probe fp_probe_1: pin names not known; wires that end beside it: adder_1_p2
  or or_3 (or_3_out, comparator_2_p4, comparator_2_p5);
  or or_4 (or_4_out[0], and_9_out, and_3_out, and_7_out);
  Register #(.width(32)) register_2 (
    .D(multiplexer_1_out), .en(or_7_out), .Q(adder_1_p2), .clk(clock_1_out));  // open: clr
  Register #(.width(32)) register_3 (
    .D(multiplexer_2_out), .en(or_8_out), .Q(register_3_q), .clk(clock_1_out));  // open: clr
  Clock clock_1 (.out(clock_1_out));
  Register #(.width(32)) register_4 (
    .D(multiplexer_3_out), .en(or_6_out), .Q(adder_1_p1), .clk(clock_1_out));  // open: clr
  not not_4 (not_4_out, or_5_out);
  // FP_Probe fp_probe_2: pin names not known; wires that end beside it: adder_1_p1
  // FP_Probe fp_probe_3: pin names not known; wires that end beside it: register_3_q
  Multiplexer #(.width(32)) multiplexer_4 (
    .in0(register_3_q), .in1(adder_1_p1), .out(multiplexer_4_out), .sel(or_8_out));  // open: en
  // FP_Const fp_const_4: pin names not known; wires that end beside it: fp_const_4_p1
  // Multiplier multiplier_1: pin names not known; wires that end beside it: multiplier_1_p1, multiplier_1_p2, multiplier_1_p3
  // FP_Const fp_const_5: pin names not known; wires that end beside it: fp_const_5_p1
  // Comparator comparator_1: pin names not known; wires that end beside it: multiplier_1_p1, fp_const_4_p1, comparator_1_p3
  // Comparator comparator_2: pin names not known; wires that end beside it: multiplier_1_p3, fp_const_4_p1, comparator_2_p3, comparator_2_p4, comparator_2_p5
  Decoder #(.select(3)) decoder_1 (
    .out0(decoder_1_out0), .out1(decoder_1_out1), .out2(decoder_1_out2), .out3(decoder_1_out3),
    .out4(decoder_1_out4), .out5(decoder_1_out5), .out6(decoder_1_out6), .out7(decoder_1_out7), .sel(or_4_out));  // open: en
  // FP_Const fp_const_6: pin names not known; wires that end beside it: fp_const_6_p1
  // FP_Const fp_const_7: pin names not known; wires that end beside it: fp_const_7_p1
  // Multiplier multiplier_2: pin names not known; wires that end beside it: fp_const_5_p1, multiplexer_4_out, multiplier_2_p3
  // Multiplier multiplier_3: pin names not known; wires that end beside it: multiplexer_4_out, multiplexer_4_out, multiplier_3_p3
  // Comparator comparator_3: pin names not known; wires that end beside it: comparator_3_p1, comparator_3_p2, comparator_3_p3, comparator_3_p4
  // Adder adder_2: pin names not known; wires that end beside it: fp_const_6_p1, multiplier_2_p3, adder_2_p3
  // Multiplier multiplier_4: pin names not known; wires that end beside it: fp_const_7_p1, multiplier_3_p3, multiplier_4_p3
  // Multiplier multiplier_5: pin names not known; wires that end beside it: multiplier_3_p3, multiplexer_4_out, multiplier_5_p3
  Multiplexer #(.width(32)) multiplexer_5 (
    .in0(multiplier_1_p1), .in1(multiplier_8_p3), .out(comparator_3_p1), .sel(comparator_1_p3));  // open: en
  // FP_Const fp_const_8: pin names not known; wires that end beside it: fp_const_8_p1
  // Multiplier multiplier_6: pin names not known; wires that end beside it: multiplier_5_p3, multiplexer_4_out, multiplier_6_p3
  // Multiplier multiplier_7: pin names not known; wires that end beside it: multiplier_6_p3, multiplexer_4_out, multiplier_7_p3
  // Multiplier multiplier_8: pin names not known; wires that end beside it: multiplier_1_p1, multiplier_8_p2, multiplier_8_p3
  // FP_Const fp_const_9: pin names not known; wires that end beside it: multiplier_8_p2
  or or_5 (or_5_out, comparator_3_p3, comparator_3_p4);
  // FP_Const fp_const_10: pin names not known; wires that end beside it: fp_const_10_p1
  // Adder adder_3: pin names not known; wires that end beside it: adder_2_p3, multiplier_4_p3, adder_3_p3
  // Multiplier multiplier_9: pin names not known; wires that end beside it: fp_const_8_p1, multiplier_5_p3, multiplier_9_p3
  // Multiplier multiplier_10: pin names not known; wires that end beside it: fp_const_10_p1, multiplier_6_p3, multiplier_10_p3
  // FP_Const fp_const_11: pin names not known; wires that end beside it: fp_const_11_p1
  // Adder adder_4: pin names not known; wires that end beside it: adder_3_p3, multiplier_9_p3, adder_4_p3
  // Multiplier multiplier_11: pin names not known; wires that end beside it: fp_const_11_p1, multiplier_7_p3, multiplier_11_p3
  Register #(.width(32)) register_5 (
    .D(adder_6_p3), .en(or_9_out), .Q(multiplier_1_p1), .clk(clock_1_out));  // open: clr
  Register #(.width(32)) register_6 (
    .D(adder_6_p3), .en(or_8_out), .Q(multiplier_1_p2), .clk(clock_1_out));  // open: clr
  or or_6 (or_6_out, decoder_1_out1, decoder_1_out6);
  // Adder adder_5: pin names not known; wires that end beside it: adder_4_p3, multiplier_10_p3, adder_5_p3
  // FP_Probe fp_probe_4: pin names not known; wires that end beside it: multiplier_1_p1
  // FP_Probe fp_probe_5: pin names not known; wires that end beside it: multiplier_1_p2
  Register #(.width(32)) register_7 (
    .D(register_3_q), .en(decoder_1_out7), .Q(register_7_q), .clk(clock_1_out));  // open: clr
  // Adder adder_6: pin names not known; wires that end beside it: adder_5_p3, multiplier_11_p3, adder_6_p3
  or or_7 (or_7_out, decoder_1_out1, decoder_1_out5);
  // FP_Probe fp_probe_6: pin names not known; wires that end beside it: register_7_q
  // FP_Const fp_const_12: pin names not known; wires that end beside it: comparator_3_p2
  // FP_Probe fp_probe_7: pin names not known; wires that end beside it: adder_6_p3
  or or_8 (or_8_out, decoder_1_out1, decoder_1_out3);
  or or_9 (or_9_out, decoder_1_out4, decoder_1_out1);

  // Notes on the sheet:
  //   P2
  //   P1
  //   P0
  //   Second Value
  //   State
  //   SSV
  //   SCV
  //   First Value
  //   FirstChanged
  //   SFV
  //   ldSV
  //   ldCV
  //   ldFV
  //   Second Value
  //   Current Value
  //   !FirstChanged
  //   First Value
  //   !Found
  //   Found
  //   CV
  //   SPC
  //   x1
  //   FV
  //   x^1
  //   ldO
  //   x^2
  //   constant
  //   x2
  //   x^3
  //   x3
  //   x^4
  //   ldCVFV
  //   ldFVFV
  //   SFV
  //   x4
  //   x^5
  //   SCV
  //   SSV
  //   x5
  //   CurrentValFonkVal
  //   FirstValFonkVal
  //   ldO
  //   ldFV
  //   ldSV
  //   limitValue
  //   ldCV & SPC & ldFVFV
  //   ldCVFV
endmodule
